# Fritzing sketch Schematic (saved by Fritzing 1.0.1rc)

parts:
  M1 = MKR ZERO
  SP1 = SPEAKER [package=pcb_mount_speaker]
  R1 = Resistor [tolerance=±5% power=0.25W resistance=100k package=THT]
  Part2 = Adafruit AMG8833 8x8 GRID EYE
  BATT1 = LiPoly Battery (1300mAh)
  Part1 = Adafruit MAX98357A I2S 3W Class D Amplifier [part_number="Adafruit #3006"]
  S1 = Toggle Switch [package=THT]

nets (from the schematic view):
  N1: M1.A6, Part1.DIN
  N2: M1.D0, S1.COM
  N3: M1.D2_PWM, Part1.BCLK
  N4: M1.D3_PWM, Part1.LRCLK
  N5: M1.D11_SDA, Part2.SDA
  N6: M1.D12_SCL, Part2.SCL
  GND: M1.GND, M1.-VBAT, R1.Pin_0, Part2.GND, BATT1.negative, Part1.GND, S1.L1
  VIN: M1.5V, Part2.VIN, Part1.VIN
  N7: M1.+VBAT, BATT1.positive
  N8: SP1.+, Part1.VO+
  N9: SP1.-, Part1.VO-
  N10: R1.Pin_1, Part1.GAIN

custom parts:
  MKR ZERO: arduino mrk zero SAMD21 Cortex-M0+ 32bit low power ARM MCU 256 meg flash 32kb sram 48mhz
  LiPoly Battery (1300mAh): Lithium Ion Polymer Battery (1300mAh)
  Adafruit MAX98357A I2S 3W Class D Amplifier: Listen to this good news - we now have an all in one digital audio amp breakout board that works incredibly well with the Raspberry Pi! If you're looking for an easy and low cost way to get you digital sound files bumpin' then the MAX08357 I2S Amp Breakout is for you. It takes standard I2S digital audio input and, not only decodes it into analog, but also amplifies it directly into a speaker.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
